# Fritzing sketch wiring (saved by Fritzing 0.7.4b)
breadboards: 1

parts:
  Arduino2 = Arduino
  U_Focus = Optocoupler [package=THT]
  U_Shutter = Optocoupler [package=THT]
  R_U_Shutter = Resistor [tolerance=±5% resistance=220 package=THT]
  R_U_Focus = Resistor [tolerance=±5% resistance=220 package=THT]
  R_LED_ON/OFF = Resistor [tolerance=±5% resistance=220 package=THT]
  S_Focus = Pushbutton [package="[THT]"]
  S_ON/OFF = Pushbutton [package="[THT]"]
  R_Remote_1 = Resistor [tolerance=±5% resistance=33k package=THT]
  R_Remote_3 = Resistor [tolerance=±5% resistance=2.2k package=THT]
  S_Shutter = Pushbutton [package="[THT]"]
  LED_ON/OFF = LED - 5mm [color="Red (633nm)" package="5 mm [THT]"]
  R_Remote_2 = Resistor [tolerance=±5% resistance=3.3k package=THT]
  U1 = mystery part, 2 pins [chip_label=Camera spacing=300mil]

nets:
  N1: Arduino2.GND, U_Focus.Pin_2, U_Shutter.Pin_2, S_ON/OFF.Pin_1, S_ON/OFF.Pin_2, LED_ON/OFF.cathode
  N2: Arduino2.D12, S_ON/OFF.Pin_3, S_ON/OFF.Pin_4
  N3: Arduino2.D11, R_LED_ON/OFF.Pin_1
  N4: Arduino2.D10, R_U_Focus.Pin_1
  N5: Arduino2.D9, R_U_Shutter.Pin_1
  N6: U_Focus.Pin_1, R_U_Focus.Pin_0
  N7: U_Focus.Pin_4, U_Shutter.Pin_4, S_Focus.Pin_3, S_Focus.Pin_4, R_Remote_1.Pin_0, S_Shutter.Pin_3, S_Shutter.Pin_4, U1.pin2
  N8: U_Focus.Pin_5, S_Focus.Pin_1, S_Focus.Pin_2, R_Remote_1.Pin_1, R_Remote_2.Pin_0
  N9: U_Shutter.Pin_1, R_U_Shutter.Pin_0
  N10: U_Shutter.Pin_5, R_Remote_3.Pin_0, S_Shutter.Pin_1, S_Shutter.Pin_2, R_Remote_2.Pin_1
  N11: R_LED_ON/OFF.Pin_0, LED_ON/OFF.anode
  N12: R_Remote_3.Pin_1, U1.pin1
